# Fritzing sketch schematics_laser_harp (saved by Fritzing 0.8.7b)
breadboards: 1

parts:
  Part1 = Arduino Uno (Rev3)
  R1 = Resistor [tolerance=±5% resistance=10k package="1206 [SMD]"]
  R2 = PHOTOCELL [package=photocell-kit]
  J1 = Piezo Speaker
  LED1 = LED - 5mm [color="Red (633nm)" package="5 mm [THT]"]  # not connected
  R3 = Resistor [tolerance=±5% resistance=10k package="1206 [SMD]"]
  Part2 = HC SR04  # not connected

nets:
  N1: Part1.A0, R1.Pin_0, R2.P$2
  N2: Part1.D2, J1.pin2
  N3: Part1.5V, R1.Pin_1
  N4: Part1.GND, R2.P$1, J1.pin1, R3.Pin_0
